# Fritzing sketch Fritzing Files of Circuit (saved by Fritzing 0.9.3b)
breadboards: 1

parts:
  S1 = Pushbutton [package="[THT]"]
  S2 = Pushbutton [package="[THT]"]
  Digispark1 = Digispark
  KY-1 = Keyes Relay [package=THT]
  KY-2 = Keyes Relay [package=THT]
  M1 = DTMF MT8870 Decoder
  R1 = Resistor [tolerance=±5% resistance=220 package="2010 [SMD]"]
  R2 = Resistor [tolerance=±5% resistance=220 package="2010 [SMD]"]

nets:
  N1: S1.Pin_1, S1.Pin_2, S2.Pin_1, S2.Pin_2, Digispark1.P0, Digispark1.P1, Digispark1.P2, Digispark1.P3, M1.Q2, M1.Q1, R1.Pin_0, R2.Pin_0
  N2: S1.Pin_3, S1.Pin_4
  N3: S2.Pin_3, S2.Pin_4
  VCC: Digispark1.VCC, KY-1.power, KY-2.power, M1.VCC
  GND: Digispark1.GND, KY-1.ground, KY-2.ground, M1.GND, R1.Pin_1, R2.Pin_1
  N4: Digispark1.P4, M1.Q3
  N5: Digispark1.P5, M1.Q4

custom parts:
  Digispark: The Digispark is an Attiny85 based microcontroller development board similar to the Arduino line, only cheaper, smaller, and a bit less powerful. With a whole host of shields to extend its functionality and the ability to use the familiar Arduino IDE the Digispark is a great way to jump into electronics, or perfect for when an Arduino is too big or too much.
  Keyes Relay: The Keyes 5V relay module is suitable for SCM development, home appliance control. It uses a 5V~12V TIL control signal which can control DC / AC signal.
  DTMF MT8870 Decoder: MT8870 DTMF voice decoding module telephone module dial control.
